// Logisim project Decoder circ.circ as structural Verilog: 1 circuit, main circuit main
module main (
  input  X,
  input  Y,
  input  Z
);

  wire a, and_1_out, and_2_out, b, c, clock_1_out, d, decoder_1_out0, decoder_1_out1, decoder_1_out2,
       decoder_1_out3, decoder_1_out4, decoder_1_out5, decoder_1_out6, decoder_1_out7, e, f, g, or_1_out,
       or_2_out;
  wire [2:0] t_ff_3_q;

  Clock clock_1 (.out(clock_1_out));
  and and_1 (and_1_out, t_ff_3_q[0], t_ff_3_q[1]);
  and and_2 (and_2_out, t_ff_3_q[2], t_ff_3_q[1]);
  T_Flip_Flop t_ff_1 (.clk(clock_1_out), .T(or_1_out), .Q(t_ff_3_q[2]));  // open: Qn, preset, reset, en
  or or_1 (or_1_out, and_1_out, and_2_out);
  T_Flip_Flop t_ff_2 (.clk(clock_1_out), .T(or_2_out), .Q(t_ff_3_q[1]));  // open: Qn, preset, reset, en
  or or_2 (or_2_out, t_ff_3_q[0], and_2_out);
  T_Flip_Flop t_ff_3 (.clk(clock_1_out), .T(1'b1), .Q(t_ff_3_q[0]));  // open: Qn, preset, reset, en
  _7_Segment_Display u_7_segment_display_1 (.g(g), .f(f), .a(a), .b(b), .e(e), .d(d), .c(c));  // open: dp
  Decoder #(.select(3)) decoder_1 (
    .out0(decoder_1_out0), .out1(decoder_1_out1), .out2(decoder_1_out2), .out3(decoder_1_out3),
    .out4(decoder_1_out4), .out5(decoder_1_out5), .out6(decoder_1_out6), .out7(decoder_1_out7),
    .sel(t_ff_3_q), .en(1'b1));
  or or_3 (a, decoder_1_out1, decoder_1_out2, decoder_1_out5, decoder_1_out6);
  or or_4 (b, decoder_1_out3, decoder_1_out4, decoder_1_out6);
  or or_5 (c, decoder_1_out2, decoder_1_out3, decoder_1_out4, decoder_1_out5);
  or or_6 (e, decoder_1_out1, decoder_1_out5, decoder_1_out6);
  or or_7 (d, decoder_1_out1, decoder_1_out2, decoder_1_out5, decoder_1_out6);
  or or_8 (f, decoder_1_out1, decoder_1_out2, decoder_1_out4, decoder_1_out5);
  or or_9 (g, decoder_1_out1, decoder_1_out2, decoder_1_out4, decoder_1_out5, decoder_1_out6);
endmodule
