// Logisim project Sequential Circuit.circ as structural Verilog: 9 circuits, main circuit main
module main (
  output out_1,
  output out_2,
  output out_3,
  output out_4,
  output out_5,
  output out_6,
  output out_7
);

  wire and_1_out, and_2_out, and_3_out, and_4_out, and_5_out, and_6_out, and_7_out, and_8_out, and_9_out,
       and_10_out, and_11_out, and_12_out, clock_1_out, j_k_ff_1_q, j_k_ff_2_q, j_k_ff_3_q, not_1_out,
       not_2_out, not_3_out, or_1_out;

  Clock clock_1 (.out(clock_1_out));
  and and_1 (and_1_out, j_k_ff_2_q, j_k_ff_3_q);
  or or_1 (or_1_out, j_k_ff_3_q, j_k_ff_1_q);
  J_K_Flip_Flop j_k_ff_1 (
    .J(and_1_out), .clk(clock_1_out), .K(j_k_ff_2_q), .Q(j_k_ff_1_q));  // open: Qn, preset, en, reset
  J_K_Flip_Flop j_k_ff_2 (
    .J(j_k_ff_3_q), .clk(clock_1_out), .K(or_1_out), .Q(j_k_ff_2_q));  // open: Qn, preset, en, reset
  J_K_Flip_Flop j_k_ff_3 (.J(1'b1), .clk(clock_1_out), .K(1'b1), .Q(j_k_ff_3_q));  // open: Qn, preset, en, reset
  not not_1 (not_1_out, j_k_ff_1_q);
  not not_2 (not_2_out, j_k_ff_2_q);
  not not_3 (not_3_out, j_k_ff_3_q);
  and and_2 (and_2_out, not_2_out, j_k_ff_3_q);
  or or_2 (out_1, and_2_out, and_3_out);
  and and_3 (and_3_out, j_k_ff_2_q, not_3_out);
  and and_4 (and_4_out, j_k_ff_1_q, not_3_out);
  or or_3 (out_2, and_4_out, and_5_out);
  and and_5 (and_5_out, j_k_ff_2_q, j_k_ff_3_q);
  and and_6 (and_6_out, not_1_out, j_k_ff_2_q);
  or or_4 (out_3, and_6_out, and_7_out);
  and and_7 (and_7_out, j_k_ff_1_q, not_2_out);
  and and_8 (and_8_out, not_2_out, j_k_ff_3_q);
  or or_5 (out_4, and_8_out, and_9_out);
  and and_9 (and_9_out, j_k_ff_2_q, not_3_out);
  and and_10 (and_10_out, not_2_out, j_k_ff_3_q);
  or or_6 (out_5, and_10_out, and_11_out);
  and and_11 (and_11_out, j_k_ff_1_q, j_k_ff_2_q);
  or or_7 (out_6, not_2_out, and_12_out);
  and and_12 (and_12_out, not_1_out, not_3_out);
  or or_8 (out_7, not_2_out, not_3_out);
  _7_Segment_Display u_7_segment_display_1 (
    .g(out_7), .f(out_6), .a(out_1), .b(out_2), .e(out_5), .d(out_4), .c(out_3));  // open: dp

  // Other names for the same wires on the sheet: a = out_1; b = out_2; c = out_3; d = out_4; e = out_5; f = out_6;
  //   g = out_7

  // Notes on the sheet:
  //   A
  //   B
  //   C
  //   X
  //   JK-Flip Flop Chosen
  //   Y
  //   Z
  //   Emon Sarker
  //   ID: 1931461642
  //   Circuit created by
  //   Combinational circuit: Simplified SOP
endmodule

module OR_GATE (
  input  GND,
  input  VCC,
  input  in_3,
  input  in_4,
  input  in_5,
  input  in_6,
  input  in_7,
  input  in_8,
  input  in_9,
  input  in_10,
  output out_11,
  output out_12,
  output out_13,
  output out_14
);

  or or_1 (out_11, in_3, in_4);
  or or_2 (out_12, in_5, in_6);
  or or_3 (out_13, in_7, in_8);
  or or_4 (out_14, in_9, in_10);
endmodule

module AND_GATE (
  input  VCC,
  input  GND,
  input  in_3,
  input  in_4,
  input  in_5,
  input  in_6,
  input  in_7,
  input  in_8,
  input  in_9,
  input  in_10,
  output out_11,
  output out_12,
  output out_13,
  output out_14
);

  and B (out_11, in_4, in_3);
  and C (out_13, in_7, in_8);
  and B_2 (out_12, in_6, in_5);
  and and_1 (out_14, in_9, in_10);
endmodule

module NOT_GATE (
  input  GND,
  input  VCC,
  input  in_3,
  input  in_4,
  input  in_5,
  input  in_6,
  input  in_7,
  input  in_8,
  output out_9,
  output out_10,
  output out_11,
  output out_12,
  output out_13,
  output out_14
);

  not not_1 (out_9, in_3);
  not not_2 (out_11, in_5);
  not not_3 (out_13, in_7);
  not not_4 (out_10, in_4);
  not not_5 (out_12, in_6);
  not not_6 (out_14, in_8);
endmodule

module NOR_GATE (
  input  GND,
  input  VCC,
  input  in_3,
  input  in_4,
  input  in_5,
  input  in_6,
  input  in_7,
  input  in_8,
  input  in_9,
  input  in_10,
  output out_11,
  output out_12,
  output out_13,
  output out_14
);

  nor nor_1 (out_11, in_3, in_4);
  nor nor_2 (out_12, in_5, in_6);
  nor nor_3 (out_13, in_7, in_8);
  nor nor_4 (out_14, in_9, in_10);
endmodule

module NAND_GATE (
  input  GND,
  input  VCC,
  input  in_3,
  input  in_4,
  input  in_5,
  input  in_6,
  input  in_7,
  input  in_8,
  input  in_9,
  input  in_10,
  output out_11,
  output out_12,
  output out_13,
  output out_14
);

  nand nand_1 (out_11, in_3, in_4);
  nand nand_2 (out_12, in_5, in_6);
  nand nand_3 (out_13, in_7, in_8);
  nand nand_4 (out_14, in_9, in_10);
endmodule

module XOR_GATE (
  input  GND,
  input  VCC,
  input  in_3,
  input  in_4,
  input  in_5,
  input  in_6,
  input  in_7,
  input  in_8,
  input  in_9,
  input  in_10,
  output out_11,
  output out_12,
  output out_13,
  output out_14
);

  xor xor_1 (out_11, in_3, in_4);
  xor xor_2 (out_12, in_5, in_6);
  xor xor_3 (out_13, in_7, in_8);
  xor xor_4 (out_14, in_9, in_10);
endmodule

module _3_input_AND_GATE (
  input  VCC,
  input  GND,
  input  in_3,
  input  in_4,
  input  in_5,
  input  in_6,
  input  in_7,
  input  in_8,
  input  in_9,
  input  in_10,
  input  in_11,
  output out_12,
  output out_13,
  output out_14
);

  and and_1 (out_12, in_3, in_4, in_5);
  and and_2 (out_13, in_6, in_7, in_8);
  and and_3 (out_14, in_9, in_10, in_11);
endmodule

module _3_input_OR_GATE (
  input  VCC,
  input  GND,
  input  in_3,
  input  in_4,
  input  in_5,
  input  in_6,
  input  in_7,
  input  in_8,
  input  in_9,
  input  in_10,
  input  in_11,
  output out_12,
  output out_13,
  output out_14
);

  or or_1 (out_12, in_3, in_4, in_5);
  or or_2 (out_13, in_6, in_7, in_8);
  or or_3 (out_14, in_9, in_10, in_11);
endmodule
